# Fritzing sketch PedalSensorsWiringDiagram (saved by Fritzing 0.9.4)
breadboards: 2

parts:
  Part1 = Adafruit Feather M0 Basic Proto [part_number="Adafruit #2772"]
  R1 = Trimmer Potentiometer [maximum_resistance=10kΩ package=THT]
  R2 = Trimmer Potentiometer [maximum_resistance=10kΩ package=THT]
  R3 = Trimmer Potentiometer [maximum_resistance=10kΩ package=THT]
  R4 = Trimmer Potentiometer [maximum_resistance=10kΩ package=THT]
  Part2 = NeoPixel Stick [part_number=1426]
  Part3 = NeoPixel Stick [part_number=1426]
  Part4 = Adafruit VL53L0X Time of Flight Distance Sensor [part_number="Adafruit #3317"]
  Part5 = Adafruit VL53L0X Time of Flight Distance Sensor [part_number="Adafruit #3317"]
  Part6 = PowerBoost 1000 Basic
  BATT1 = LiPoly Battery (1300mAh)  # not connected

nets:
  GND: Part1.GND, R1.leg1, R2.leg1, Part2.GND, Part3.GND, Part4.GND, Part5.GND, Part6.GND
  N1: Part1.A4, R4.wiper
  N2: Part1.A3, R3.wiper
  N3: Part1.A2, R2.wiper
  N4: Part1.A1, R1.wiper
  VIN: Part1.+3V3, R1.leg2, R2.leg2, Part4.VIN, Part5.VIN
  N5: Part1.VBAT, Part6.VBAT
  N6: Part1.D13, Part2.DATAIN
  N7: Part1.D6, Part4.XSHUT
  N8: Part1.D5, Part5.XSHUT
  N9: Part1.SCL, Part4.SCL, Part5.SCL
  N10: Part1.SDA, Part4.SDA, Part5.SDA
  N11: Part2.DATAOUT, Part3.DATAIN
  +5V: Part2.+5V, Part3.+5V, Part6.5.0V

custom parts:
  Adafruit Feather M0 Basic Proto: At the Feather M0's heart is an ATSAMD21G18 ARM Cortex M0 processor, clocked at 48 MHz and at 3.3V logic, the same one used in the new Arduino Zero. This chip has a whopping 256K of FLASH (8x more than the Atmega328 or 32u4) and 32K of RAM (16x as much)! This chip comes with built in USB so it has USB-to-Serial program & debug capability built in with no need for an FTDI-like chip. To make it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
  NeoPixel Stick: Make your own little LED strip arrangement with this stick of NeoPixel LEDs. We crammed 8 of the tiny 5050 (5mm x 5mm) smart RGB LEDs onto a PCB with mounting holes and a chainable design. Use only one microcontroller pin to control as many as you can chain together! Each LED is addressable as the driver chip is inside the LED. Each one has ~18mA constant current drive so the color will be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
  Adafruit VL53L0X Time of Flight Distance Sensor: The VL53L0X is a Time of Flight distance sensor like no other you've used! The sensor contains a very tiny invisible laser source, and a matching sensor. The VL53L0X can detect the "time of flight", or how long the light has taken to bounce back to the sensor. Since it uses a very narrow light source, it is good for determining distance of only the surface directly in front of it. Unlike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
  PowerBoost 1000 Basic: The PowerBoost 1000 is a little DC/DC boost converter module that can run from 1.8V batteries or higher, and convert the battery output to 5.2V DC for running your 5V projects. At its heart is a TPS61030 boost converter from TI. This boost converter chip has some really nice extras such as low battery detection, 4A internal switch, synchronous conversion, excellent efficiency, and 700KHz high-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
  LiPoly Battery (1300mAh): Lithium Ion Polymer Battery (1300mAh)
