# Fritzing sketch PedalSensorsWiringDiagram_NoBooster (saved by Fritzing 0.9.4)
breadboards: 2

parts:
  Part1 = Adafruit Feather M0 Basic Proto [part_number="Adafruit #2772"]
  Part2 = NeoPixel Stick [part_number=1426]
  Part3 = NeoPixel Stick [part_number=1426]
  Part4 = Adafruit VL53L0X Time of Flight Distance Sensor [part_number="Adafruit #3317"]
  Part5 = Adafruit VL53L0X Time of Flight Distance Sensor [part_number="Adafruit #3317"]
  BATT1 = LiPoly Battery (1300mAh)  # not connected
  S1 = Toggle Switch [package=THT]
  S2 = Pushbutton [package="[THT]"]
  S3 = Pushbutton [package="[THT]"]
  S4 = Pushbutton [package="[THT]"]
  S5 = Pushbutton [package="[THT]"]
  R1 = Resistor [tolerance=±5% resistance=10k package=THT]
  R2 = Resistor [tolerance=±5% resistance=10k package=THT]
  R3 = Resistor [tolerance=±5% resistance=10k package=THT]
  R4 = Resistor [tolerance=±5% resistance=10k package=THT]
  R5 = Trimmer Potentiometer [maximum_resistance=10kΩ package=THT]

nets:
  N1: Part1.A5, S5.Pin_1, S5.Pin_2, R4.Pin_0
  N2: Part1.A3, S4.Pin_1, S4.Pin_2, R3.Pin_0
  N3: Part1.A2, R5.wiper
  N4: Part1.A1, S3.Pin_1, S3.Pin_2, R2.Pin_0
  N5: Part1.A0, S2.Pin_1, S2.Pin_2, R1.Pin_0
  GND: Part1.GND, Part2.GND, Part3.GND, Part4.GND, Part5.GND, S1.L2, S4.Pin_3, S4.Pin_4, S5.Pin_3, S5.Pin_4, R1.Pin_1, R2.Pin_1, R3.Pin_1, R4.Pin_1, R5.leg2
  +5V: Part1.+3V3, Part2.+5V, Part3.+5V, Part4.VIN, Part5.VIN, S2.Pin_3, S2.Pin_4, S3.Pin_3, S3.Pin_4, R5.leg1
  N6: Part1.EN, S1.COM
  N7: Part1.D13, Part2.DATAIN
  N8: Part1.D6, Part4.XSHUT
  N9: Part1.D5, Part5.XSHUT
  N10: Part1.SCL, Part4.SCL, Part5.SCL
  N11: Part1.SDA, Part4.SDA, Part5.SDA
  N12: Part2.DATAOUT, Part3.DATAIN

custom parts:
  Adafruit Feather M0 Basic Proto: At the Feather M0's heart is an ATSAMD21G18 ARM Cortex M0 processor, clocked at 48 MHz and at 3.3V logic, the same one used in the new Arduino Zero. This chip has a whopping 256K of FLASH (8x more than the Atmega328 or 32u4) and 32K of RAM (16x as much)! This chip comes with built in USB so it has USB-to-Serial program & debug capability built in with no need for an FTDI-like chip. To make it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
  NeoPixel Stick: Make your own little LED strip arrangement with this stick of NeoPixel LEDs. We crammed 8 of the tiny 5050 (5mm x 5mm) smart RGB LEDs onto a PCB with mounting holes and a chainable design. Use only one microcontroller pin to control as many as you can chain together! Each LED is addressable as the driver chip is inside the LED. Each one has ~18mA constant current drive so the color will be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
  Adafruit VL53L0X Time of Flight Distance Sensor: The VL53L0X is a Time of Flight distance sensor like no other you've used! The sensor contains a very tiny invisible laser source, and a matching sensor. The VL53L0X can detect the "time of flight", or how long the light has taken to bounce back to the sensor. Since it uses a very narrow light source, it is good for determining distance of only the surface directly in front of it. Unlike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
  LiPoly Battery (1300mAh): Lithium Ion Polymer Battery (1300mAh)
